// Digital circuit Clock.dig as structural Verilog
module Clock (
  input  Fast,
  input  Slow,
  input  Watch,
  output CLK,
  output CLK_2
);

  wire _7402_1_pin1, _7402_1_pin2, _7402_1_pin3, _7402_1_pin6, _7402_1_pin8, _7402_1_pin9, _7402_1_pin10,
       _7402_1_pin12, _74151_1_pin4;

  _7402 _7402_1 (
    .pin1(_7402_1_pin1), .pin2(_7402_1_pin2), .pin3(_7402_1_pin3), .pin4(_7402_1_pin3), .pin5(_7402_1_pin1),
    .pin6(_7402_1_pin6), .pin7(1'b0), .pin8(_7402_1_pin8), .pin9(_7402_1_pin9), .pin10(_7402_1_pin10),
    .pin11(_7402_1_pin10), .pin12(_7402_1_pin12), .pin13(_7402_1_pin9), .pin14(1'b1));
  // SwitchDT Debug_Run: pin names not known; wires that end beside it: _7402_1_pin12, 1'b1, _7402_1_pin8
  // SwitchDT Slow_Fast: pin names not known; wires that end beside it: _7402_1_pin2, 1'b1, _7402_1_pin6
  LED led_1 (.in(_7402_1_pin9));
  LED led_2 (.in(_7402_1_pin1));
  _74151 _74151_1 (
    .pin1(Fast), .pin2(Slow), .pin3(Watch), .pin4(_74151_1_pin4), .pin5(CLK), .pin6(CLK_2), .pin7(1'b0),
    .pin8(1'b0), .pin9(1'b0), .pin10(_7402_1_pin9), .pin11(_7402_1_pin1), .pin12(1'b0), .pin13(1'b0),
    .pin14(1'b0), .pin15(1'b0), .pin16(1'b1));
  Button Step (.out(_74151_1_pin4));

  // Notes on the sheet:
  //   Fast: Hz: 10
  //   Slow: Hz: 4
endmodule
