// Digital circuit dasPuter.dig as structural Verilog
module dasPuter (
  input  clk,
  input  clk_2,
  input  clk_3
);

  wire button_1_out, switchdt_1_p2, switchdt_1_p3, switchdt_2_p2, switchdt_2_p3, switchdt_2_p4, switchdt_2_p5;

  Button button_1 (.out(button_1_out));
  // SwitchDT switchdt_1: pin names not known; wires that end beside it: 1'b1, switchdt_1_p2, switchdt_1_p3
  // SwitchDT switchdt_2: pin names not known; wires that end beside it: 1'b1, switchdt_2_p2, switchdt_2_p3, switchdt_2_p4, switchdt_2_p5
  Clock clock_1 (
    .Debug(switchdt_1_p2), .Run(switchdt_1_p3), .Slow(switchdt_2_p2), .Fast(switchdt_2_p3),
    .Step(button_1_out), .WCLK(clk_3), .SCLK(clk_2), .FCLK(clk), .CLK(switchdt_2_p4), .CLK_2(switchdt_2_p5));
  LED u_CLK (.in(switchdt_2_p4));
  LED u_CLK_2 (.in(switchdt_2_p5));

  // Notes on the sheet:
  //   clk: Hz: 10
  //   clk_2: Hz: 4
endmodule
