// Digital circuit Memory.dig as structural Verilog
module Memory (
  input  PCINCR,
  input  BUS0,
  input  BUS1,
  input  BUS2,
  input  BUS3
);

  // _74173 _74173_1: pin names not known
  // _74283 _74283_1: pin names not known
  // _74157 _74157_1: pin names not known; wires that end beside it: BUS1, BUS0
endmodule
