// Digital circuit PC.dig as structural Verilog
module PC (
  input  RST,
  input  CLK,
  input  PCO,
  input  PCI,
  input  BUS0,
  input  BUS1,
  input  BUS2,
  input  BUS3,
  input  BUS4,
  input  BUS5,
  input  BUS6,
  input  BUS7,
  input  PCE,
  output PC7,
  output PC6,
  output PC5,
  output PC4,
  output PC3,
  output PC2,
  output PC1,
  output PC0
);

  wire _74161_1_pin15;

  _74161 _74161_1 (
    .pin1(RST), .pin2(CLK), .pin3(BUS0), .pin4(BUS1), .pin5(BUS2), .pin6(BUS3), .pin7(PCE), .pin8(1'b0),
    .pin9(PCI), .pin10(1'b1), .pin11(PC3), .pin12(PC2), .pin13(PC1), .pin14(PC0), .pin15(_74161_1_pin15),
    .pin16(1'b1));
  _74161 _74161_2 (
    .pin1(RST), .pin2(CLK), .pin3(BUS4), .pin4(BUS5), .pin5(BUS6), .pin6(BUS7), .pin7(PCE), .pin8(1'b0),
    .pin9(PCI), .pin10(_74161_1_pin15), .pin11(PC7), .pin12(PC6), .pin13(PC5), .pin14(PC4), .pin16(1'b1));  // open: pin15
  _74244 _74244_1 (
    .pin1(PCO), .pin2(PC0), .pin3(BUS7), .pin4(PC1), .pin5(BUS6), .pin6(PC2), .pin7(BUS5), .pin8(PC3),
    .pin9(BUS4), .pin10(1'b0), .pin11(PC4), .pin12(BUS3), .pin13(PC5), .pin14(BUS2), .pin15(PC6),
    .pin16(BUS1), .pin17(PC7), .pin18(BUS0), .pin19(PCO), .pin20(1'b1));
endmodule
